# Fritzing sketch Sketch (saved by Fritzing 0.9.9b)

parts:
  M1 = ESP32 FIREBEETLE IOT V3 [part_number=ESP32_FIREBEETLE]
  U1 = LIPO-110mAh [package=lipo-110]
  J1 = JST-03JQ-BT [part_number=JST-JQ-BT package=THT]

nets:
  N1: M1.GND, M1.LIPO-, U1.-, J1.pin2
  N2: M1.VCC, M1.LIPO+, U1.+, J1.pin1
  N3: M1.A0/IO36, J1.pin3

notes:
  Flow meter

custom parts:
  ESP32 FIREBEETLE IOT V3: DFRobot Firebeetle ESP32 IOT Microcontroller V3, 36-Pin ESP32.
